# Fritzing sketch mega (saved by Fritzing 0.9.0b)
breadboards: 1

parts:
  MEGA = Arduino Mega 2560 (Rev3)
  NRF24L01 = NRF24L01
  C3 = Capacitor Polarized [package=cpol-radial-10uf-25v]
  MAX9814 = Adafruit MAX9814 Electret Microphone Amplifier [part_number="Adafruit #1713"]

nets:
  N1: MEGA.A0, MAX9814.OUTPUT
  GND: MEGA.GND, NRF24L01.GND, C3.-, MAX9814.GND
  3V3: MEGA.3V3, NRF24L01.VCC, C3.+, MAX9814.VDD, MAX9814.GAIN
  N2: MEGA.D40, NRF24L01.CE
  N3: MEGA.D50, NRF24L01.MISO
  N4: MEGA.D51, NRF24L01.MOSI
  N5: MEGA.D52, NRF24L01.SCK
  N6: MEGA.D53, NRF24L01.CSN

custom parts:
  NRF24L01: NRF24L01 module
  Adafruit MAX9814 Electret Microphone Amplifier: Add an ear to your project with this well-designed electret microphone amplifier with AGC. This fully assembled and tested board comes with a 20-20KHz electret microphone soldered on. For the amplification, we use the Maxim MAX9814, a specialty chip that is designed for amplifying electret microphones in situations where the loudness of the audio isn't predictable. This fancy microphone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
