# Fritzing sketch nano (saved by Fritzing 0.9.0b)
breadboards: 1

parts:
  Part1 = Arduino Nano (Rev3.0)
  NRF24L1 = NRF24L01
  C2 = Capacitor Polarized [package=cpol-radial-10uf-25v]
  GY1 = MPU-6050 Board GY-521 [form="♀ (female)" package=THT]

nets:
  GND: Part1.GND, NRF24L1.GND, C2.-, GY1.pin2
  N1: Part1.D2, GY1.pin7, GY1.pin8
  N2: Part1.D9, NRF24L1.CE
  N3: Part1.D10, NRF24L1.CSN
  N4: Part1.D11/MOSI, NRF24L1.MOSI
  N5: Part1.D12/MISO, NRF24L1.MISO
  N6: Part1.A5, GY1.pin3
  N7: Part1.A4, GY1.pin4
  3V3: Part1.3V3, NRF24L1.VCC, C2.+, GY1.pin1
  N8: Part1.D13/SCK, NRF24L1.SCK

custom parts:
  NRF24L01: NRF24L01 module
  MPU-6050 Board GY-521: Acelerometro y Giroscopio MPU-6050 Board GY-521
